# Fritzing sketch menorah (saved by Fritzing 0.9.3b)
breadboards: 1

parts:
  Part1 = Arduino Uno (Rev3)
  LED1 = LED - 5mm [color="Blue (430nm)" current=20mA package="5 mm [THT]"]
  R1 = Resistor [tolerance=±5% resistance=100 package=THT]
  LED2 = LED - 5mm [color="White (4500K)" current=20mA package="5 mm [THT]"]
  R2 = Resistor [tolerance=±5% resistance=100 package=THT]
  R3 = Resistor [tolerance=±5% resistance=100 package=THT]
  R4 = Resistor [tolerance=±5% resistance=100 package=THT]
  R5 = Resistor [tolerance=±5% resistance=100 package=THT]
  R6 = Resistor [tolerance=±5% resistance=100 package=THT]
  R7 = Resistor [tolerance=±5% resistance=100 package=THT]
  R8 = Resistor [tolerance=±5% resistance=100 package=THT]
  R9 = Resistor [tolerance=±5% resistance=100 package=THT]
  LED3 = LED - 5mm [color="White (4500K)" current=20mA package="5 mm [THT]"]
  LED4 = LED - 5mm [color="White (4500K)" current=20mA package="5 mm [THT]"]
  LED5 = LED - 5mm [color="White (4500K)" current=20mA package="5 mm [THT]"]
  LED6 = LED - 5mm [color="White (4500K)" current=20mA package="5 mm [THT]"]
  LED7 = LED - 5mm [color="White (4500K)" current=20mA package="5 mm [THT]"]
  LED8 = LED - 5mm [color="White (4500K)" current=20mA package="5 mm [THT]"]
  LED9 = LED - 5mm [color="White (4500K)" current=20mA package="5 mm [THT]"]
  R10 = Resistor [tolerance=±5% resistance=100 package=THT]
  S1 = Toggle Switch [package=THT]
  S2 = Toggle Switch [package=THT]
  S3 = Toggle Switch [package=THT]
  S4 = Toggle Switch [package=THT]
  R11 = Resistor [tolerance=±5% resistance=100 package=THT]

nets:
  N1: Part1.A0, S3.COM
  N2: Part1.A1, S2.COM
  N3: Part1.A2, S1.COM
  N4: Part1.A5/SCL, S4.COM
  N5: Part1.D8, R3.Pin_1
  N6: Part1.D9_PWM, R2.Pin_1
  N7: Part1.D13/SCK, R1.Pin_1
  N8: Part1.GND, LED1.cathode, LED2.cathode, LED3.cathode, LED4.cathode, LED5.cathode, LED6.cathode, LED7.cathode, LED8.cathode, LED9.cathode, S1.L1, S2.L1, S3.L1, S4.L1
  N9: Part1.D2, R9.Pin_1
  N10: Part1.D3_PWM, R8.Pin_1
  N11: Part1.D4, R7.Pin_1
  N12: Part1.D5_PWM, R6.Pin_1
  N13: Part1.D6_PWM, R5.Pin_1
  N14: Part1.D7, R4.Pin_1
  N15: Part1.5V, R10.Pin_0, R11.Pin_0
  N16: LED1.anode, R1.Pin_0
  N17: LED2.anode, R2.Pin_0
  N18: R3.Pin_0, LED3.anode
  N19: R4.Pin_0, LED4.anode
  N20: R5.Pin_0, LED5.anode
  N21: R6.Pin_0, LED6.anode
  N22: R7.Pin_0, LED7.anode
  N23: R8.Pin_0, LED8.anode
  N24: R9.Pin_0, LED9.anode
  N25: R10.Pin_1, S1.L2, S2.L2, S3.L2
  N26: S4.L2, R11.Pin_1
